# Fritzing sketch Drivhuset (saved by Fritzing 0.9.3b)

parts:
  Raspberry_Pi_1 = Raspberry Pi 3 [part_number=RPI-3-V1.2]
  Part1 = ADS1015
  Part2 = Jtron 1 Channel Optoisolated Relay Module [package=relay]
  Part3 = FC-28 Soil Hygrometer Module
  Part4 = Soil Moisture Sensor
  M1 = DC Motor
  R1 = Photocell (LDR) [package=THT]  # not connected

nets:
  VCC: Raspberry_Pi_1.3v3, Part1.VDD, Part2.VCC, Part3.VCC
  N1: Raspberry_Pi_1.GPIO2, Part1.SDA
  N2: Raspberry_Pi_1.GPIO3, Part1.SCL
  N3: Raspberry_Pi_1.GPIO4, Part2.IN1
  GND: Raspberry_Pi_1.GND, Part1.GND, Part2.GND, Part3.GND
  N4: Part1.A0, Part3.AO
  N5: Part2.NC, M1.pin_1
  N6: Part2.MAIN, M1.pin_2
  N7: Part3.POS, Part4.VCC
  N8: Part3.NEG, Part4.SIG

custom parts:
  ADS1015: ADC ADS1015
  FC-28 Soil Hygrometer Module: The FC-28 is a soil hygrometer module that uses the Texas Instruments LM393 comparator chip to provide an analog measurement of soil humidity. The digital output is high when soil moisture is over a certain threshold, as determined by adjusting the potentiometer.
